# Fritzing sketch schematic (saved by Fritzing 0.8.7b)
breadboards: 1

parts:
  U3 = HC-SR04 [chip_label=IC package="SIP (Single Inline) [THT]"]
  Part1 = Arduino Uno (Rev3)
  LCD1 = LCD screen
  R1 = Trimmer Potentiometer [maximum_resistance=10kΩ package=THT]

nets:
  VCC: U3.Vcc, Part1.5V, LCD1.VDD, LCD1.LED+, R1.leg1
  N1: U3.Trig, Part1.D12/MISO
  N2: U3.Echo, Part1.D11_PWM/MOSI
  GND: U3.GND, Part1.GND, LCD1.VSS, LCD1.R/W, LCD1.LED-, R1.leg2
  N3: Part1.D2, LCD1.RS
  N4: Part1.D3_PWM, LCD1.E
  N5: Part1.D4, LCD1.DB4
  N6: Part1.D5_PWM, LCD1.DB5
  N7: Part1.D6_PWM, LCD1.DB6
  N8: Part1.D7, LCD1.DB7
  N9: LCD1.V0, R1.wiper

custom parts:
  HC-SR04: HC-SR04 ultrasound distance sensor
